# Fritzing sketch Untitled Sketch (saved by Fritzing 0.9.6b)
breadboards: 1

parts:
  A1 = Raspberry Pi 5
  USBTTL1 = USB A Plug
  SERVO1 = Tower Pro SG90 servo [part_number=101246]
  SERVO2 = Tower Pro SG90 servo [part_number=101246]
  Part1 = GY-VL53L0XV2 Laser Ranger Module
  J1 = Generic female header - 1 pins [form="♀ (female)" package=THT]
  USBTTL2 = USB A Plug
  J2 = Piezo Speaker

nets:
  3V3: A1.3V3, Part1.VCC
  +5V: A1.5V, A1.Fan-5V, SERVO1.+5V, SERVO2.+5V
  N1: A1.GPIO2, Part1.SDA
  N2: A1.GPIO3, Part1.SCL
  GND: A1.GND, A1.Fan-GND, SERVO1.GND, SERVO2.GND, Part1.GND
  N3: A1.GPIO17, SERVO1.Signal
  N4: A1.GPIO27, SERVO2.Signal
  N5: USBTTL1.usb, J1.pin1, USBTTL2.usb, J2.pin1

custom parts:
  Raspberry Pi 5: The RPi5, a faster version of the awesome Raspberry Pi4B ARM Board with 40 pin gpio.
  Tower Pro SG90 servo: Original file by John De Cristofaro http://www.adafruit.com/products/1449 Adafruit Feedback Servo (Small) Edited by: e-radionica.com 28/9/2015
  GY-VL53L0XV2 Laser Ranger Module: The GY-VL53L0XV2 is based on the VL53L0X from ST Microelectronics, a time-of-flight ranging system integrated into a compact module.
  Generic female header - 1 pins: Generic female header
